// Logisim project ROCK_SCISSORS_PAPER.circ as structural Verilog: 6 circuits, main circuit main
module main (
  input  S1,
  input  S2,
  input  S3,
  input  S4,
  output [1:0] out_5,
  output [1:0] out_6,
  output [2:0] Win_Count_P,
  output Player_P_Win,
  output Player_Q_Win,
  output [2:0] Win_Count_Q,
  output Tie
);

  wire RESET_out, selector_1_p_wins, selector_1_q_wins;
  wire [3:0] bit_extender_1_out, bit_extender_2_out;

  Button RESET (.out(RESET_out));
  Dec dec_1 (.S1(S1), .S2(S2), .S3(S3), .S4(S4), .Player_P(out_5), .Player_Q(out_6));
  selector selector_1 (
    .S1(S1), .S2(S2), .S3(S3), .S4(S4), .P_wins(selector_1_p_wins), .Q_wins(selector_1_q_wins), .Tie(Tie));
  Counter_P counter_p_1 (
    .P_wins(selector_1_p_wins), .Clear(RESET_out), .Q0(Win_Count_P[0]), .Q1(Win_Count_P[1]),
    .Q2(Win_Count_P[2]));
  Counter_Q counter_q_1 (
    .Q_wins(selector_1_q_wins), .Clear(RESET_out), .Q0(Win_Count_Q[0]), .Q1(Win_Count_Q[1]),
    .Q2(Win_Count_Q[2]));
  assign bit_extender_1_out = {{1{1'b0}}, Win_Count_P};  // Bit_Extender bit_extender_1
  Hex_Digit_Display #(.decimalPoint("false")) hex_digit_display_1 (.value(bit_extender_1_out));
  assign bit_extender_2_out = {{1{1'b0}}, Win_Count_Q};  // Bit_Extender bit_extender_2
  Hex_Digit_Display #(.decimalPoint("false")) hex_digit_display_2 (.value(bit_extender_2_out));
  Comp comp_1 (.Q0(Win_Count_P[0]), .Q1(Win_Count_P[1]), .Q2(Win_Count_P[2]), .Player_Wins(Player_P_Win));
  Comp comp_2 (.Q0(Win_Count_Q[0]), .Q1(Win_Count_Q[1]), .Q2(Win_Count_Q[2]), .Player_Wins(Player_Q_Win));
  LED led_1 (.in(Player_P_Win));
  LED led_2 (.in(Player_Q_Win));
  LED led_3 (.in(Tie));

  // Notes on the sheet:
  //   RESET WHEN ANY PLAYER WINS
endmodule

module Dec (
  input  S1,
  input  S2,
  input  S3,
  input  S4,
  output [1:0] Player_P,
  output [1:0] Player_Q
);

  wire decoder_1_out2, decoder_1_out3, decoder_2_out2, decoder_2_out3;

  Decoder #(.enable("false"), .select(2)) decoder_1 (
    .out0(Player_P[0]), .out1(Player_P[1]), .out2(decoder_1_out2), .out3(decoder_1_out3), .sel({S2, S1}));
  Decoder #(.enable("false"), .select(2)) decoder_2 (
    .out0(Player_Q[0]), .out1(Player_Q[1]), .out2(decoder_2_out2), .out3(decoder_2_out3), .sel({S4, S3}));
endmodule

module selector (
  input  S1,
  input  S2,
  input  S3,
  input  S4,
  output P_wins,
  output Q_wins,
  output Tie
);

  wire and_1_out, and_2_out, and_3_out, and_4_out, and_5_out, and_6_out, and_7_out, and_8_out, and_9_out;

  and and_1 (and_1_out, ~S1, ~S2, ~S3, S4);  // AND_Gate
  and and_2 (and_2_out, ~S1, S2, S3, ~S4);  // AND_Gate
  and and_3 (and_3_out, S1, ~S2, ~S3, ~S4);  // AND_Gate
  and and_4 (and_4_out, ~S1, ~S2, S3, ~S4);  // AND_Gate
  and and_5 (and_5_out, ~S1, S2, ~S3, ~S4);  // AND_Gate
  and and_6 (and_6_out, S1, ~S2, ~S3, S4);  // AND_Gate
  and and_7 (and_7_out, ~S1, ~S2, ~S3, ~S4);  // AND_Gate
  and and_8 (and_8_out, S1, ~S2, S3, ~S4);  // AND_Gate
  and and_9 (and_9_out, ~S1, S2, ~S3, S4);  // AND_Gate
  or or_1 (P_wins, and_1_out, and_2_out, and_3_out);
  or or_2 (Q_wins, and_4_out, and_5_out, and_6_out);
  or or_3 (Tie, and_7_out, and_8_out, and_9_out);
endmodule

module Counter_P (
  input  P_wins,
  input  Clear,
  output Q0,
  output Q1,
  output Q2
);

  wire clock_1_out;

  Counter #(.max('h7), .width(3)) counter_1 (
    .count(P_wins), .Q({Q2, Q1, Q0}), .clk(clock_1_out), .clr(Clear));  // open: load, D, carry, up
  Clock clock_1 (.out(clock_1_out));
endmodule

module Counter_Q (
  input  Q_wins,
  input  Clear,
  output Q0,
  output Q1,
  output Q2
);

  wire clock_1_out;

  Counter #(.max('h7), .width(3)) counter_1 (
    .count(Q_wins), .Q({Q2, Q1, Q0}), .clk(clock_1_out), .clr(Clear));  // open: load, D, carry, up
  Clock clock_1 (.out(clock_1_out));
endmodule

module Comp (
  input  Q0,
  input  Q1,
  input  Q2,
  output Player_Wins
);

  and and_1 (Player_Wins, ~Q0, ~Q1, Q2);  // AND_Gate
endmodule
